# Fritzing sketch esp8266_speech (saved by Fritzing 0.9.3b)
circuit board: 8.46667cm x 5.64444cm
breadboards: 1

parts:
  Part4 = Breakout Board for Electret Microphone
  Part3 = SparkFun ESP8266 Thing
  MCP320 = IC, DIP package, 8 pins [chip_label=MCP3201]
  C1 = Tantalum Capacitor [capacitance=1μF package="100 mil [THT, tantalum]"]

nets:
  VCC: Part4.VCC, Part3.VCC, MCP320.pin1, MCP320.pin8
  GND: Part4.GND, Part3.GND, MCP320.pin3, C1.-
  N1: Part4.AUD, MCP320.pin2, C1.+
  N2: Part3.GPIO14, MCP320.pin7
  N3: Part3.GPIO12, MCP320.pin6
  N4: Part3.GPIO15, MCP320.pin5
